// Logisim project ABS2022.circ as structural Verilog: 1 circuit, main circuit main
module main (
  input  wheel,
  output unlock
);

  wire and_1_out, and_2_out, and_3_out, and_4_out, and_5_out, and_6_out, and_7_out, clock_1_out, or_1_out,
       or_2_out, S0_q, S1_q;

  Clock clock_1 (.out(clock_1_out));
  and and_1 (and_1_out, ~S1_q, S0_q, ~wheel);  // AND_Gate
  and and_2 (and_2_out, S1_q, ~S0_q);  // AND_Gate
  and and_3 (and_3_out, ~S1_q, ~S0_q, ~wheel);  // AND_Gate
  and and_4 (and_4_out, S1_q, ~S0_q);  // AND_Gate
  D_Flip_Flop S1 (.D(or_1_out), .clk(clock_1_out), .Q(S1_q));  // open: Qn, preset, reset
  or or_1 (or_1_out, and_1_out, and_2_out);
  D_Flip_Flop S0 (.D(or_2_out), .clk(clock_1_out), .Q(S0_q));  // open: Qn, preset, reset
  or or_2 (or_2_out, and_3_out, and_4_out);
  and and_5 (and_5_out, ~S1_q, ~S0_q, ~wheel);  // AND_Gate
  and and_6 (and_6_out, ~S1_q, S0_q, ~wheel);  // AND_Gate
  and and_7 (and_7_out, S1_q, ~S0_q);  // AND_Gate
  or or_3 (unlock, and_5_out, and_6_out, and_7_out);

  // Notes on the sheet:
  //   s0
  //   s1
  //   wheel
  //   ABS; in class example
endmodule
