// Logisim project Class_Examples.circ as structural Verilog: 2 circuits, main circuit cs1_26
module cs1_26 (
  input  A,
  input  B,
  output notA,
  output A_and_B,
  output A_OR_B
);

  and and_1 (A_and_B, A, B);
  or or_1 (A_OR_B, A, B);
  not not_1 (notA, A);

  // Notes on the sheet:
  //   AND
  //   NOT
  //   OR
  //   Circuit w/ 3 outputs
endmodule

module LU (
  input  in_1,
  input  in_2
);

  wire cs1_26_1_nota;

  cs1_26 cs1_26_1 (.A(in_1), .B(in_2), .notA(cs1_26_1_nota));  // open: A_and_B, A_OR_B
  Register register_1 (.clr(cs1_26_1_nota));  // open: D, en, clk, Q

  // Notes on the sheet:
  //   testing stuff: 1/26
endmodule
