// Logisim project fsm_circ_inclass.circ as structural Verilog: 2 circuits, main circuit my_try
module my_try (
  output [3:0] out_1
);

  wire clock_1_out;
  wire [3:0] adder_1_out, register_1_q, undriven;

  Clock clock_1 (.out(clock_1_out));
  // Buffer buffer_1 is placed but not wired
  Adder #(.width(4)) adder_1 (.a(register_1_q), .b(undriven), .out(adder_1_out));  // open: cin, cout
  Register #(.width(4)) register_1 (.D(adder_1_out), .clk(clock_1_out), .Q(register_1_q));  // open: en, clr
  Comparator comparator_1 ();  // open: a, b, gt, eq, lt
endmodule

module JD_circ (
  input  in_put,
  output out_put
);

  wire clock_1_out, decoder_1_out0, decoder_1_out1;
  wire [1:0] counter_1_q;

  Clock clock_1 (.out(clock_1_out));
  Decoder #(.enable("false")) decoder_1 (.out0(decoder_1_out0), .out1(decoder_1_out1), .sel(in_put));
  Counter #(.max('h3), .width(2)) counter_1 (
    .clr(decoder_1_out0), .clk(clock_1_out), .Q(counter_1_q));  // open: load, up, count, D, carry
  Comparator #(.width(2)) comparator_1 (.a(counter_1_q), .b(2'b11), .eq(out_put));  // open: gt, lt

  // Notes on the sheet:
  //   decoder = if/else
  //   diff. if 0 or 1
  //   --> also works w/ not gate
  //   reset
endmodule
