// Logisim project her_pogil.circ as structural Verilog: 1 circuit, main circuit main
module main (
  input  [2:0] in_1,
  input  in_2,
  input  in_3,
  input  [15:0] R1,
  input  [15:0] R2,
  input  [2:0] in_6,
  output [15:0] R3,
  output out_8,
  output out_9
);

  wire decoder_2_out3, decoder_2_out4, decoder_2_out5, decoder_2_out6, decoder_2_out7;

  Divider divider_1 ();  // open: a, b, out, upper, rem
  // Decoder #(.enable("false")) decoder_1: pin names not known; wires that end beside it: R1, R2
  Adder #(.width(16)) adder_1 ();  // open: a, b, out, cin, cout
  // AND_Gate and_1 is placed but not wired
  // OR_Gate or_1 is placed but not wired
  // XOR_Gate xor_1 is placed but not wired
  Subtractor subtractor_1 ();  // open: a, b, out, bin, bout
  Decoder #(.enable("false"), .select(3)) decoder_2 (
    .out3(decoder_2_out3), .out4(decoder_2_out4), .out5(decoder_2_out5), .out6(decoder_2_out6),
    .out7(decoder_2_out7), .sel(in_1));  // open: out0, out1, out2
  Multiplexer #(.select(3)) multiplexer_1 (
    .in0(in_2), .in1(in_2), .in2(in_2), .in3(in_3), .in4(in_3), .in5(in_3), .in6(in_3), .in7(in_3),
    .out(out_9), .sel(in_6));
  or or_2 (out_8, decoder_2_out3, decoder_2_out4, decoder_2_out5, decoder_2_out6, decoder_2_out7);
  Multiplexer #(.width(16)) multiplexer_2 ();  // open: in0, in1, out, sel

  // Notes on the sheet:
  //   ADD(R3, R1, R2)
  //   HERA : POGIL
  //   decoder: which thing is active
endmodule
