// Logisim project miniHera.circ as structural Verilog: 3 circuits, main circuit regBank
module regBank (
  input  [3:0] d,
  input  [3:0] a,
  input  [3:0] b,
  input  [15:0] Rd,
  input  clk,
  output [15:0] Ra,
  output [15:0] Rb
);

  wire decoder_1_out0, decoder_1_out1, decoder_1_out2, decoder_1_out3;
  wire [15:0] R0_q, R1_q, R2_q, R3_q;

  Decoder #(.select(4)) decoder_1 (
    .out0(decoder_1_out0), .out1(decoder_1_out1), .out2(decoder_1_out2), .out3(decoder_1_out3), .sel(d));  // open: out4, out5, out6, out7, out8, out9, out10, out11, out12, out13, out14, out15, en
  Register #(.width(16)) R0 (.D(Rd), .en(decoder_1_out0), .clk(clk), .Q(R0_q));  // open: clr
  Register #(.width(16)) R1 (.D(Rd), .en(decoder_1_out1), .clk(clk), .Q(R1_q));  // open: clr
  Register #(.width(16)) R2 (.D(Rd), .en(decoder_1_out2), .clk(clk), .Q(R2_q));  // open: clr
  Register #(.width(16)) R3 (.D(Rd), .en(decoder_1_out3), .clk(clk), .Q(R3_q));  // open: clr
  Multiplexer #(.select(4), .width(16)) multiplexer_1 (
    .in0(R0_q), .in1(R1_q), .in2(R2_q), .in3(R3_q), .out(Ra), .sel(a));  // open: in4, in5, in6, in7, in8, in9, in10, in11, in12, in13, in14, in15
  Multiplexer #(.select(4), .width(16)) multiplexer_2 (
    .in0(R0_q), .in1(R1_q), .in2(R2_q), .in3(R3_q), .out(Rb), .sel(b));  // open: in4, in5, in6, in7, in8, in9, in10, in11, in12, in13, in14, in15

  // Notes on the sheet:
  //   d input = instruction for which register to write to
  //   using decoder to enable the correct register based on d
  //   mux based on a, putting what's in register into Ra
endmodule

module main (
);

  wire clock_1_out;
  wire [15:0] alsu_1_rd, instruction, regbank_1_ra, regbank_1_rb;

  Clock clock_1 (.out(clock_1_out));
  ROM #(.addrWidth(16), .dataWidth(16)) rom_1 (.addr({16{1'b0}}), .data(instruction));
  regBank regbank_1 (
    .d(instruction[11:8]), .a(instruction[7:4]), .b(instruction[3:0]), .Rd(alsu_1_rd), .clk(clock_1_out),
    .Ra(regbank_1_ra), .Rb(regbank_1_rb));
  ALSU alsu_1 (.Ra(regbank_1_ra), .Rb(regbank_1_rb), .opcode(instruction[15:12]), .Rd(alsu_1_rd));

  // Other names for the same wires on the sheet: opcode[3:0] = instruction[15:12]

  // Notes on the sheet:
  //   contents of rom_1 (hex, n*v repeats v):
  //   8321
endmodule

module ALSU (
  input  [15:0] Ra,
  input  [15:0] Rb,
  input  [3:0] opcode,
  output [15:0] Rd
);

  wire [15:0] and_1_out;

  assign and_1_out = Ra & Rb;  // AND_Gate and_1, 16 bits wide
  Multiplexer #(.select(4), .width(16)) multiplexer_1 (
    .in8(and_1_out), .out(Rd), .sel(opcode));  // open: in0, in1, in2, in3, in4, in5, in6, in7, in9, in10, in11, in12, in13, in14, in15
endmodule
