// Logisim project lab0_circuit.circ as structural Verilog: 2 circuits, main circuit XOR4bit
module XOR4bit (
  input  in_1,
  input  A,
  input  in_3,
  input  in_4,
  input  in_5,
  input  B,
  input  in_7,
  input  in_8,
  output out_9,
  output out_10,
  output out_11,
  output out_12
);

  wire and_1_out, and_2_out, and_3_out, and_4_out, and_5_out, and_6_out, and_7_out, and_8_out, not_1_out,
       not_2_out, not_3_out, not_4_out, not_5_out, not_6_out, not_7_out, not_8_out;

  not not_1 (not_1_out, in_1);
  not not_2 (not_2_out, in_5);
  not not_3 (not_3_out, A);
  not not_4 (not_4_out, B);
  not not_5 (not_5_out, in_3);
  not not_6 (not_6_out, in_7);
  not not_7 (not_7_out, in_4);
  not not_8 (not_8_out, in_8);
  and and_1 (and_1_out, not_1_out, in_5);
  and and_2 (and_2_out, in_1, not_2_out);
  and and_3 (and_3_out, not_3_out, B);
  and and_4 (and_4_out, A, not_4_out);
  and and_5 (and_5_out, not_5_out, in_7);
  and and_6 (and_6_out, in_3, not_6_out);
  and and_7 (and_7_out, not_7_out, in_8);
  and and_8 (and_8_out, in_4, not_8_out);
  or or_1 (out_9, and_1_out, and_2_out);
  or or_2 (out_10, and_3_out, and_4_out);
  or or_3 (out_11, and_5_out, and_6_out);
  or or_4 (out_12, and_7_out, and_8_out);

  // Notes on the sheet:
  //   NOT
  //   NOT
  //   NOT
  //   NOT
  //   NOT
  //   NOT
  //   NOT
  //   NOT
  //   AND
  //   AND
  //   AND
  //   AND
  //   AND
  //   AND
  //   AND
  //   AND
  //   4-bit XOR Circuit
  //   OR
  //   OR
  //   OR
  //   OR
  //   Output: Y
endmodule

module proof (
  input  in_1,
  input  A,
  input  in_3,
  input  in_4,
  input  in_5,
  input  B,
  input  in_7,
  input  in_8,
  output out_9,
  output out_10,
  output Output__A,
  output out_12
);

  wire XOR_4bit_out_9, XOR_4bit_out_10, XOR_4bit_out_11, XOR_4bit_out_12;

  XOR4bit XOR_4bit (
    .in_1(in_1), .A(A), .in_3(in_3), .in_4(in_4), .in_5(in_5), .B(B), .in_7(in_7), .in_8(in_8),
    .out_9(XOR_4bit_out_9), .out_10(XOR_4bit_out_10), .out_11(XOR_4bit_out_11), .out_12(XOR_4bit_out_12));
  XOR4bit XOR_4bt (
    .in_1(XOR_4bit_out_9), .A(XOR_4bit_out_10), .in_3(XOR_4bit_out_11), .in_4(XOR_4bit_out_12), .in_5(in_5),
    .B(B), .in_7(in_7), .in_8(in_8), .out_9(out_9), .out_10(out_10), .out_11(Output__A), .out_12(out_12));

  // Notes on the sheet:
  //   Proof for ((a XOR b) XOR b) == a
endmodule
