// Logisim project lab02.circ as structural Verilog: 5 circuits, main circuit half_adder
module half_adder (
  input  a,
  input  b,
  output sum,
  output carry
);

  and and_1 (carry, a, b);
  xor xor_1 (sum, a, b);

  // Notes on the sheet:
  //   Half-Adder
  //   XOR
  //   AND
endmodule

module one_bit_full_adder (
  input  carry_in,
  input  a,
  input  b,
  output sum,
  output carry_out
);

  wire half_adder_1_carry, half_adder_1_sum, half_adder_2_carry;

  half_adder half_adder_1 (.a(a), .b(b), .sum(half_adder_1_sum), .carry(half_adder_1_carry));
  half_adder half_adder_2 (.a(carry_in), .b(half_adder_1_sum), .sum(sum), .carry(half_adder_2_carry));
  or or_1 (carry_out, half_adder_2_carry, half_adder_1_carry);

  // Notes on the sheet:
  //   Full adder
  //   OR
endmodule

module four_bit_full_adder (
  input  [3:0] b_4_bit,
  input  [3:0] a_4_bit,
  output [3:0] out_4_bit,
  output carry_out
);

  wire half_adder_1_carry, one_bit_full_adder_1_carry_out, one_bit_full_adder_2_carry_out;

  half_adder half_adder_1 (.a(a_4_bit[0]), .b(b_4_bit[0]), .sum(out_4_bit[0]), .carry(half_adder_1_carry));
  one_bit_full_adder one_bit_full_adder_1 (
    .carry_in(half_adder_1_carry), .a(a_4_bit[1]), .b(b_4_bit[1]), .sum(out_4_bit[1]),
    .carry_out(one_bit_full_adder_1_carry_out));
  one_bit_full_adder one_bit_full_adder_2 (
    .carry_in(one_bit_full_adder_1_carry_out), .a(a_4_bit[2]), .b(b_4_bit[2]), .sum(out_4_bit[2]),
    .carry_out(one_bit_full_adder_2_carry_out));
  one_bit_full_adder one_bit_full_adder_3 (
    .carry_in(one_bit_full_adder_2_carry_out), .a(a_4_bit[3]), .b(b_4_bit[3]), .sum(out_4_bit[3]),
    .carry_out(carry_out));

  // Notes on the sheet:
  //   4 bit full adder
  //   d.) the number of gates in the full adder is 17
  //   this number comes from the 2 gates in the half adder and the 5 gates in each full adder
  //   sorry that a and b are reversed! I saw tha they were wired wrong too late and thought it would be easiest to just switch the labels
endmodule

module adder_subtractor (
  input  Add_Substract,
  input  [3:0] a_4_bit,
  input  [3:0] b_4_bit,
  output [3:0] out_put,
  output carry_out,
  output over_flow
);

  wire four_bit_full_adder_ver_2_1_prev_carry_out;
  wire [3:0] xor_1_out;

  xor xor_1 (xor_1_out[0], Add_Substract, b_4_bit[0]);
  xor xor_2 (xor_1_out[1], Add_Substract, b_4_bit[1]);
  xor xor_3 (xor_1_out[2], Add_Substract, b_4_bit[2]);
  xor xor_4 (xor_1_out[3], Add_Substract, b_4_bit[3]);
  four_bit_full_adder_ver_2 four_bit_full_adder_ver_2_1 (
    .add_subtract(Add_Substract), .a_4_bit(a_4_bit), .b_4_bit(xor_1_out), .out_4_bit(out_put),
    .prev_carry_out(four_bit_full_adder_ver_2_1_prev_carry_out), .carry_out(carry_out));
  xor xor_5 (over_flow, four_bit_full_adder_ver_2_1_prev_carry_out, carry_out);

  // Notes on the sheet:
  //   4 bit Adder-Subtractor
  //   XOR
  //   XOR
  //   Two's complement above
  //   XOR
  //   XOR
  //   d.) the number of gates being used is 18 - number of gates in four bit full adder + 1 for the XOR gate
  //   The number of total gates (including the two's complement which are being unused) is 22.
  //   XOR
endmodule

module four_bit_full_adder_ver_2 (
  input  add_subtract,
  input  [3:0] a_4_bit,
  input  [3:0] b_4_bit,
  output [3:0] out_4_bit,
  output prev_carry_out,
  output carry_out
);

  wire one_bit_full_adder_1_carry_out, one_bit_full_adder_2_carry_out;

  one_bit_full_adder one_bit_full_adder_1 (
    .carry_in(add_subtract), .a(a_4_bit[0]), .b(b_4_bit[0]), .sum(out_4_bit[0]),
    .carry_out(one_bit_full_adder_1_carry_out));
  one_bit_full_adder one_bit_full_adder_2 (
    .carry_in(one_bit_full_adder_1_carry_out), .a(a_4_bit[1]), .b(b_4_bit[1]), .sum(out_4_bit[1]),
    .carry_out(one_bit_full_adder_2_carry_out));
  one_bit_full_adder one_bit_full_adder_3 (
    .carry_in(one_bit_full_adder_2_carry_out), .a(a_4_bit[2]), .b(b_4_bit[2]), .sum(out_4_bit[2]),
    .carry_out(prev_carry_out));
  one_bit_full_adder one_bit_full_adder_4 (
    .carry_in(prev_carry_out), .a(a_4_bit[3]), .b(b_4_bit[3]), .sum(out_4_bit[3]), .carry_out(carry_out));

  // Notes on the sheet:
  //   circuit for the adder-subtractor
  //   (difference from actual 4 bit full ader is a half adder in beginning & another output to get 3rd carry)
  //   need this carry output to figure out overflow
endmodule
