// Logisim project lab2.circ as structural Verilog: 6 circuits, main circuit written_hw
module written_hw (
  input  A,
  input  B,
  input  C,
  output X
);

  wire nand_1_out, nand_2_out, nand_3_out, nand_4_out, not_1_out, not_2_out, not_3_out;

  not not_1 (not_1_out, A);
  not not_2 (not_2_out, B);
  not not_3 (not_3_out, C);
  nand nand_1 (nand_1_out, not_1_out, not_2_out);
  nand nand_2 (nand_2_out, not_1_out, B);
  nand nand_3 (nand_3_out, A, not_3_out);
  nand nand_4 (nand_4_out, A, B, C);
  nand nand_5 (X, nand_1_out, nand_2_out, nand_3_out, nand_4_out);

  // Notes on the sheet:
  //   NAND
  //   NAND
  //   NAND
  //   NAND
  //   2 level NAND gate circuit
  //   For sum of products
  //   NAND
endmodule

module vending_mach (
  input  q,
  input  d0,
  input  d1,
  input  d2,
  output Vend,
  output n_2,
  output n_1,
  output n_0
);

  vend_output vend_output_1 (.q(q), .d0(d0), .d1(d1), .d2(d2), .Vend(Vend));
  nickel_2 nickel_2_1 (.q(q), .d0(d0), .d1(d1), .d2(d2), .n_2(n_2));
  nickel_1 nickel_1_1 (.q(q), .d0(d0), .d1(d1), .d2(d2), .n_1(n_1));
  nickel_0 nickel_0_1 (.q(q), .n_0(n_0));

  // Notes on the sheet:
  //   Full Vending Machine
endmodule

module vend_output (
  input  q,
  input  d0,
  input  d1,
  input  d2,
  output Vend
);

  wire and_1_out, and_2_out, and_3_out, and_4_out, not_1_out, not_2_out, not_3_out;

  not not_1 (not_1_out, q);
  not not_2 (not_2_out, d0);
  not not_3 (not_3_out, d1);
  and and_1 (and_1_out, not_1_out, d0, d1, d2);
  and and_2 (and_2_out, q, d0);
  and and_3 (and_3_out, q, not_2_out, d1);
  and and_4 (and_4_out, q, not_2_out, not_3_out, d2);
  or or_1 (Vend, and_1_out, and_2_out, and_3_out, and_4_out);

  // Notes on the sheet:
  //   AND
  //   AND
  //   AND
  //   AND
  //   Output for Vending Machine
  //   (Getting item or not)
  //   OR
endmodule

module nickel_0 (
  input  q,
  output n_0
);


  assign n_0 = q;

  // Notes on the sheet:
  //   Outout for vending machine
  //   (single nickel as change)
endmodule

module nickel_1 (
  input  q,
  input  d0,
  input  d1,
  input  d2,
  output n_1
);

  wire and_1_out, and_2_out, and_3_out, and_4_out, and_5_out, and_6_out, not_1_out, not_2_out, not_3_out,
       not_4_out;

  not not_1 (not_1_out, d2);
  not not_2 (not_2_out, d1);
  not not_3 (not_3_out, d0);
  not not_4 (not_4_out, q);
  and and_1 (and_1_out, not_4_out, not_3_out, not_2_out, d2);
  and and_2 (and_2_out, not_4_out, not_3_out, d1, not_1_out);
  and and_3 (and_3_out, not_4_out, d0, not_2_out, not_1_out);
  and and_4 (and_4_out, q, not_3_out, d1, d2);
  and and_5 (and_5_out, q, d0, not_2_out, d2);
  and and_6 (and_6_out, q, d0, d1, not_1_out);
  or or_1 (n_1, and_1_out, and_2_out, and_3_out, and_4_out, and_5_out, and_6_out);

  // Notes on the sheet:
  //   AND
  //   AND
  //   AND
  //   AND
  //   AND
  //   AND
  //   Output for Vending Machine
  //   (seeing if there's 2 nickels as change)
  //   OR
endmodule

module nickel_2 (
  input  q,
  input  d0,
  input  d1,
  input  d2,
  output n_2
);

  wire and_1_out, and_2_out, and_3_out, and_4_out, and_5_out, not_1_out, not_2_out, not_3_out, not_4_out;

  not not_1 (not_1_out, d2);
  not not_2 (not_2_out, d0);
  not not_3 (not_3_out, d1);
  not not_4 (not_4_out, q);
  and and_1 (and_1_out, not_4_out, not_2_out, d1, d2);
  and and_2 (and_2_out, not_4_out, d0, not_3_out, d2);
  and and_3 (and_3_out, not_4_out, d0, d1, not_1_out);
  and and_4 (and_4_out, q, not_2_out, not_3_out, not_1_out);
  and and_5 (and_5_out, q, d0, d1, d2);
  or or_1 (n_2, and_1_out, and_2_out, and_3_out, and_4_out, and_5_out);

  // Notes on the sheet:
  //   AND
  //   AND
  //   AND
  //   AND
  //   AND
  //   Output for Vending Machine
  //   (seeing if there's 4 nickels as change)
  //   OR
endmodule
