// Logisim project lab03.circ as structural Verilog: 10 circuits, main circuit main
module main (
  input  in_put,
  input  re_set,
  output is_vend,
  output [2:0] change
);

  wire clk_out, first_state_pri_1_s_one, second_state_pri_1_s_two, state_0_q, state_1_q, state_2_q,
       zero_state_pri_1_s_zero;
  wire [2:0] outputs_1_nickels, reset_1_rst_change;

  Clock clk (.out(clk_out));
  second_state_pri second_state_pri_1 (
    .s2(state_2_q), .s1(state_1_q), .s0(state_0_q), .q_d(in_put), .s_two(second_state_pri_1_s_two));
  first_state_pri first_state_pri_1 (
    .s2(state_2_q), .s1(state_1_q), .s0(state_0_q), .q_d(in_put), .s_one(first_state_pri_1_s_one));
  zero_state_pri zero_state_pri_1 (
    .s2(state_2_q), .s1(state_1_q), .s0(state_0_q), .q_d(in_put), .s_zero(zero_state_pri_1_s_zero));
  D_Flip_Flop state_2 (.D(second_state_pri_1_s_two), .clk(clk_out), .Q(state_2_q), .reset(re_set));  // open: Qn, preset
  D_Flip_Flop state_1 (.D(first_state_pri_1_s_one), .clk(clk_out), .Q(state_1_q), .reset(re_set));  // open: Qn, preset
  D_Flip_Flop state_0 (.D(zero_state_pri_1_s_zero), .clk(clk_out), .Q(state_0_q), .reset(re_set));  // open: Qn, preset
  reset reset_1 (
    .state_2(second_state_pri_1_s_two), .state_1(first_state_pri_1_s_one), .state_0(zero_state_pri_1_s_zero),
    .re_set(re_set), .clock(clk_out), .rst_change(reset_1_rst_change));
  outputs outputs_1 (
    .state_2(state_2_q), .state_1(state_1_q), .state_0(state_0_q), .is_vend(is_vend),
    .nickels(outputs_1_nickels));
  assign change = outputs_1_nickels | reset_1_rst_change;  // OR_Gate or_1, 3 bits wide

  // Notes on the sheet:
  //   Vending Machine!
endmodule

module second_state_pri (
  input  s2,
  input  s1,
  input  s0,
  input  q_d,
  output s_two
);

  wire and_1_out, and_2_out, and_3_out, and_4_out, and_5_out, not_1_out;

  not not_1 (not_1_out, q_d);
  and and_1 (and_1_out, ~s2, ~s1, s0, ~q_d, not_1_out);  // AND_Gate
  and and_2 (and_2_out, ~s2, s1, s0, ~q_d, not_1_out);  // AND_Gate
  and and_3 (and_3_out, ~s2, s1, s0, q_d, ~not_1_out);  // AND_Gate
  and and_4 (and_4_out, s2, ~s1, s0, ~q_d, not_1_out);  // AND_Gate
  and and_5 (and_5_out, s2, ~s1, s0, q_d, ~not_1_out);  // AND_Gate
  or or_1 (s_two, and_1_out, and_2_out, and_3_out, and_4_out, and_5_out);

  // Notes on the sheet:
  //   S2' logic
endmodule

module first_state_pri (
  input  s2,
  input  s1,
  input  s0,
  input  q_d,
  output s_one
);

  wire and_1_out, and_2_out, and_3_out, and_4_out, and_5_out, and_6_out, and_7_out, and_8_out, not_1_out;

  not not_1 (not_1_out, q_d);
  and and_1 (and_1_out, ~s2, ~s1, ~s0, ~q_d, not_1_out);  // AND_Gate
  and and_2 (and_2_out, ~s2, ~s1, s0, q_d, ~not_1_out);  // AND_Gate
  and and_3 (and_3_out, ~s2, s1, ~s0, ~q_d, not_1_out);  // AND_Gate
  and and_4 (and_4_out, s2, ~s1, ~s0, ~q_d, not_1_out);  // AND_Gate
  and and_5 (and_5_out, s2, ~s1, s0, ~q_d, not_1_out);  // AND_Gate
  and and_6 (and_6_out, s2, ~s1, s0, q_d, ~not_1_out);  // AND_Gate
  and and_7 (and_7_out, s2, s1, ~s0, ~q_d, not_1_out);  // AND_Gate
  and and_8 (and_8_out, s2, s1, s0, ~q_d, not_1_out);  // AND_Gate
  or or_1 (s_one, and_1_out, and_2_out, and_3_out, and_4_out, and_5_out, and_6_out, and_7_out, and_8_out);

  // Notes on the sheet:
  //   S1' logic
endmodule

module zero_state_pri (
  input  s2,
  input  s1,
  input  s0,
  input  q_d,
  output s_zero
);

  wire not_1_out, or_1_out, or_2_out, or_3_out, or_4_out;

  not not_1 (not_1_out, q_d);
  or or_1 (or_1_out, s2, s1, ~s0, q_d, ~not_1_out);  // OR_Gate
  or or_2 (or_2_out, s2, s1, ~s0, ~q_d, not_1_out);  // OR_Gate
  or or_3 (or_3_out, s2, ~s1, ~s0, ~q_d, not_1_out);  // OR_Gate
  or or_4 (or_4_out, ~s2, s1, ~s0, q_d, ~not_1_out);  // OR_Gate
  and and_1 (s_zero, or_1_out, or_2_out, or_3_out, or_4_out);

  // Notes on the sheet:
  //   S0' logic
endmodule

module vend (
  input  state_2,
  input  state_1,
  input  state_0,
  output vending
);

  wire and_1_out, and_2_out, and_3_out, and_4_out;

  and and_1 (and_1_out, ~state_2, state_1, ~state_0);  // AND_Gate
  and and_2 (and_2_out, state_2, ~state_1, ~state_0);  // AND_Gate
  and and_3 (and_3_out, state_2, state_1, ~state_0);  // AND_Gate
  and and_4 (and_4_out, state_2, state_1, state_0);
  or or_1 (vending, and_1_out, and_2_out, and_3_out, and_4_out);

  // Notes on the sheet:
  //   Seeing if vending or not
endmodule

module nickel_2ndbit (
  input  state_2,
  input  state_1,
  input  state_0,
  output nickel_2ndbt
);

  wire and_1_out, and_2_out, and_3_out;

  and and_1 (and_1_out, ~state_2, ~state_1, state_0);  // AND_Gate
  and and_2 (and_2_out, ~state_2, state_1, ~state_0);  // AND_Gate
  or or_1 (nickel_2ndbt, and_1_out, and_2_out, and_3_out);
  and and_3 (and_3_out, state_2, ~state_1, state_0);  // AND_Gate

  // Notes on the sheet:
  //   change: 2nd bit
endmodule

module nickel_1stbit (
  input  state_2,
  input  state_1,
  input  state_0,
  output nickel_1stbt
);

  wire and_1_out, and_2_out;

  and and_1 (and_1_out, ~state_2, state_1, state_0);  // AND_Gate
  and and_2 (and_2_out, state_2, state_1, state_0);
  or or_1 (nickel_1stbt, and_1_out, and_2_out);

  // Notes on the sheet:
  //   change = 1st bit
endmodule

module nickel_0thbit (
  input  state_2,
  input  state_1,
  input  state_0,
  output nickel_0thbt
);

  wire and_1_out, and_2_out, and_3_out;

  and and_1 (and_1_out, ~state_2, ~state_1, state_0);  // AND_Gate
  and and_2 (and_2_out, state_2, ~state_1, ~state_0);  // AND_Gate
  and and_3 (and_3_out, state_2, state_1, state_0);
  or or_1 (nickel_0thbt, and_1_out, and_2_out, and_3_out);

  // Notes on the sheet:
  //   change = 0th bit
endmodule

module reset (
  input  state_2,
  input  state_1,
  input  state_0,
  input  re_set,
  input  clock,
  output [2:0] rst_change
);

  wire and_1_out, d_ff_1_q, d_ff_2_q, d_ff_3_q, not_1_out;

  not not_1 (not_1_out, re_set);
  D_Flip_Flop d_ff_1 (.D(state_2), .clk(re_set), .Q(d_ff_1_q), .reset(and_1_out));  // open: Qn, preset
  and and_1 (and_1_out, not_1_out, clock);
  D_Flip_Flop d_ff_2 (.D(state_1), .clk(re_set), .Q(d_ff_2_q), .reset(and_1_out));  // open: Qn, preset
  D_Flip_Flop d_ff_3 (.D(state_0), .clk(re_set), .Q(d_ff_3_q), .reset(and_1_out));  // open: Qn, preset
  nickel_2ndbit ni_2ndbt (.state_2(d_ff_1_q), .state_1(d_ff_2_q), .state_0(d_ff_3_q), .nickel_2ndbt(rst_change[2]));
  nickel_1stbit ni_1stbt (.state_2(d_ff_1_q), .state_1(d_ff_2_q), .state_0(d_ff_3_q), .nickel_1stbt(rst_change[1]));
  nickel_0thbit ni_0thbt (.state_2(d_ff_1_q), .state_1(d_ff_2_q), .state_0(d_ff_3_q), .nickel_0thbt(rst_change[0]));

  // Notes on the sheet:
  //   logic for reset
  //   3.) Resetting the flip flops
  //   Process
  //   1.) load each new state into these flip flops
  //   2a.) if Reset = 0 (not clicked), overwrite with new state
  //   resets when reset is 0 (in main circuit) and clock is 0 
  //   2b.) if Reset = 1 (clicked), calculate the change in nickels using the states stored in the flip flops
  //   Is resetting in order to clear the memory in the d flip flops and thus setting change as zero 
endmodule

module outputs (
  input  state_2,
  input  state_1,
  input  state_0,
  output is_vend,
  output [2:0] nickels
);

  wire n_0_nickel_0thbt, n_1_nickel_1stbt, n_2_nickel_2ndbt;

  vend vending (.state_2(state_2), .state_1(state_1), .state_0(state_0), .vending(is_vend));
  nickel_2ndbit n_2 (.state_2(state_2), .state_1(state_1), .state_0(state_0), .nickel_2ndbt(n_2_nickel_2ndbt));
  nickel_1stbit n_1 (.state_2(state_2), .state_1(state_1), .state_0(state_0), .nickel_1stbt(n_1_nickel_1stbt));
  nickel_0thbit n_0 (.state_2(state_2), .state_1(state_1), .state_0(state_0), .nickel_0thbt(n_0_nickel_0thbt));
  and and_1 (nickels[2], n_2_nickel_2ndbt, is_vend);
  and and_2 (nickels[1], n_1_nickel_1stbt, is_vend);
  and and_3 (nickels[0], n_0_nickel_0thbt, is_vend);

  // Notes on the sheet:
  //   Logic for outputs of vending machine
  //   note: keeping track of change in each state but only outputs change when vending
  //   if sufficient amount of coins, will vend 
  //   if vend, then will also output change (so that way shifting to state 0)
endmodule
