// Logisim project lab4.circ as structural Verilog: 2 circuits, main circuit main
module main (
);

  wire clk_out, comparator_1_gt, comparator_1_lt;
  wire [2:0] counter_1_q, rom3by4_1_out_2_2;
  wire [3:0] adder_1_out, and_1_out, and_2_out, multiplexer_1_out, or_1_out, R1_q, R2_q, subtractor_1_out,
       subtractor_2_out, xor_1_out;
  wire [3:3] rom3by4_1_out_2;

  Clock clk (.out(clk_out));
  Counter #(.max('h7), .width(3)) counter_1 (.clk(clk_out), .Q(counter_1_q));  // open: clr, load, up, count, D, carry
  ROM3by4 rom3by4_1 (.in_1(counter_1_q), .out_2({rom3by4_1_out_2[3], rom3by4_1_out_2_2}));
  Comparator #(.mode("unsigned"), .width(4)) comparator_1 (
    .a({rom3by4_1_out_2[3], rom3by4_1_out_2_2}), .b(4'b0111), .gt(comparator_1_gt), .lt(comparator_1_lt));  // open: eq
  Register #(.width(4)) R1 (
    .D({rom3by4_1_out_2[3], rom3by4_1_out_2_2}), .en(comparator_1_lt), .clk(clk_out), .Q(R1_q));  // open: clr
  Register #(.width(4)) R2 (.D(R1_q), .en(comparator_1_lt), .clk(clk_out), .Q(R2_q));  // open: clr
  assign and_1_out = R1_q & R2_q;  // AND_Gate and_1, 4 bits wide
  assign or_1_out = R1_q | R2_q;  // OR_Gate or_1, 4 bits wide
  Adder #(.width(4)) adder_1 (.a(R1_q), .b(R2_q), .out(adder_1_out));  // open: cin, cout
  Subtractor #(.width(4)) subtractor_1 (.a(R1_q), .b(R2_q), .out(subtractor_1_out));  // open: bin, bout
  assign xor_1_out = R1_q ^ R2_q;  // XOR_Gate xor_1, 4 bits wide
  Subtractor #(.width(4)) subtractor_2 (.a(R2_q), .b(R1_q), .out(subtractor_2_out));  // open: bin, bout
  Multiplexer #(.select(3), .width(4)) multiplexer_1 (
    .in0(and_1_out), .in1(or_1_out), .in2(adder_1_out), .in3(subtractor_1_out), .in5(xor_1_out),
    .in7(subtractor_2_out), .out(multiplexer_1_out), .sel(rom3by4_1_out_2_2));  // open: in4, in6
  and and_2 (and_2_out[0], multiplexer_1_out[0], comparator_1_gt);
  and and_3 (and_2_out[1], multiplexer_1_out[1], comparator_1_gt);
  and and_4 (and_2_out[2], multiplexer_1_out[2], comparator_1_gt);
  and and_5 (and_2_out[3], multiplexer_1_out[3], comparator_1_gt);
  Hex_Digit_Display #(.decimalPoint("false")) hex_digit_display_1 (.value(and_2_out));

  // Notes on the sheet:
  //   3 bit counter
  //   process:
  //   Values are put into comparator 
  //   using my ROM
  //   Counter goes through values in ROM
  //   greater than 7:  mux to select & output
  //   less than 7: can write to register & anything in R1 put into R2
  //   *uses AND gates to make sure only >7 values displayed
  //   AND
  //   SUB
  //   OR
  //   XOR
  //   ADD
  //   SUB
  //   getting rid of most significant bit for select bit
  //   now, select bit corresponds to 4 bit MUX
  //   else, displays 0
  //   AND
  //   AND
  //   AND
  //   AND
  //   making sure displaying if num > 7 in ROM
endmodule

module ROM3by4 (
  input  [2:0] in_1,
  output [3:0] out_2
);

  Multiplexer #(.select(3), .width(4)) multiplexer_1 (
    .in0(4'b0101), .in1(4'b0011), .in2(4'b1111), .in3(4'b1010), .in4(4'b0000), .in5(4'b0000), .in6(4'b0000),
    .in7(4'b0000), .out(out_2), .sel(in_1));

  // Notes on the sheet:
  //   ROM : 4 bit
  //   counter val
  //   Process:
  //   num from ROM
  //   depending on counter value, gets a number from ROM (via MUX) and outputs number at address
endmodule
