// Logisim project HERA.circ as structural Verilog: 10 circuits, main circuit main
module main (
);

  wire clk;
  wire [3:0] a, b, d;
  wire [4:0] alsu_1_flags_out, flags_1_flags_out;
  wire [15:0] address, R1, R2, R3, Rd, reg_bank_1_ra, reg_bank_1_rb;
  wire [15:12] instruction;

  Clock clock_1 (.out(clk));
  Counter #(.max('hffff), .width(16)) counter_1 (.clk(clk), .Q(address));  // open: clr, load, up, count, D, carry
  Hex_Digit_Display hex_digit_display_1 (.value(address[15:12]));  // open: dp
  Hex_Digit_Display hex_digit_display_2 (.value(address[11:8]));  // open: dp
  Hex_Digit_Display hex_digit_display_3 (.value(address[7:4]));  // open: dp
  ROM #(.addrWidth(16), .dataWidth(16)) rom_1 (.addr(address), .data({instruction, d, a, b}));
  Hex_Digit_Display hex_digit_display_4 (.value(address[3:0]));  // open: dp
  reg_bank reg_bank_1 (
    .d(d), .a(a), .b(b), .Rd(Rd), .clk(clk), .Ra(reg_bank_1_ra), .Rb(reg_bank_1_rb), .R_1(R1), .R_2(R2),
    .R_3(R3));
  Hex_Digit_Display hex_digit_display_5 (.value(instruction));  // open: dp
  Hex_Digit_Display hex_digit_display_6 (.value(d));  // open: dp
  Hex_Digit_Display hex_digit_display_7 (.value(a));  // open: dp
  Hex_Digit_Display hex_digit_display_8 (.value(b));  // open: dp
  Hex_Digit_Display hex_digit_display_9 (.value(R1[15:12]));  // open: dp
  Hex_Digit_Display hex_digit_display_10 (.value(R1[11:8]));  // open: dp
  Hex_Digit_Display hex_digit_display_11 (.value(R1[7:4]));  // open: dp
  ALSU alsu_1 (
    .Ra(reg_bank_1_ra), .Rb(reg_bank_1_rb), .R_d(Rd), .b(b), .a(a), .d(d), .opcode(instruction),
    .flags_in(flags_1_flags_out), .Rd(Rd), .flags_out(alsu_1_flags_out));
  Hex_Digit_Display hex_digit_display_12 (.value(R1[3:0]));  // open: dp
  Hex_Digit_Display hex_digit_display_13 (.value(R2[15:12]));  // open: dp
  Hex_Digit_Display hex_digit_display_14 (.value(R2[11:8]));  // open: dp
  Hex_Digit_Display hex_digit_display_15 (.value(R2[7:4]));  // open: dp
  Hex_Digit_Display hex_digit_display_16 (.value(R2[3:0]));  // open: dp
  flags flags_1 (.clock(clk), .flags_in(alsu_1_flags_out), .flags_out(flags_1_flags_out));
  Hex_Digit_Display hex_digit_display_17 (.value(R3[15:12]));  // open: dp
  DotMatrix #(.matrixrows(1)) dotmatrix_1 (
    .col0(flags_1_flags_out[0]), .col1(flags_1_flags_out[1]), .col2(flags_1_flags_out[2]),
    .col3(flags_1_flags_out[3]), .col4(flags_1_flags_out[4]));
  Hex_Digit_Display hex_digit_display_18 (.value(R3[11:8]));  // open: dp
  Hex_Digit_Display hex_digit_display_19 (.value(R3[7:4]));  // open: dp
  Hex_Digit_Display hex_digit_display_20 (.value(R3[3:0]));  // open: dp

  // Other names for the same wires on the sheet: instruction[11:0] = {d, a, b}; opcode[3:0] = instruction

  // Notes on the sheet:
  //   current_address
  //   contents of rom_1 (hex, n*v repeats v):
  //   3160 e12a f100 3101 57638*0 f
  //   current_instruction
  //   R1
  //   R2
  //   sign
  //   zero
  //   Flag display
  //   overflow
  //   R3
  //   carry
  //   CBON()
endmodule

module reg_bank (
  input  [3:0] d,
  input  [3:0] a,
  input  [3:0] b,
  input  [15:0] Rd,
  input  clk,
  output [15:0] Ra,
  output [15:0] Rb,
  output [15:0] R_1,
  output [15:0] R_2,
  output [15:0] R_3
);

  wire decoder_1_out1, decoder_1_out2, decoder_1_out3, decoder_1_out4, decoder_1_out5, decoder_1_out6,
       decoder_1_out7, decoder_1_out8, decoder_1_out9, decoder_1_out10, decoder_1_out11, decoder_1_out12,
       decoder_1_out13, decoder_1_out14, decoder_1_out15;
  wire [15:0] R4, R5, R6, R7, R8, R9, R10, R11, R12, R13, R14, R15;

  Decoder #(.select(4)) decoder_1 (
    .out1(decoder_1_out1), .out2(decoder_1_out2), .out3(decoder_1_out3), .out4(decoder_1_out4),
    .out5(decoder_1_out5), .out6(decoder_1_out6), .out7(decoder_1_out7), .out8(decoder_1_out8),
    .out9(decoder_1_out9), .out10(decoder_1_out10), .out11(decoder_1_out11), .out12(decoder_1_out12),
    .out13(decoder_1_out13), .out14(decoder_1_out14), .out15(decoder_1_out15), .sel(d));  // open: out0, en
  Register #(.width(16)) R1 (.D(Rd), .en(decoder_1_out1), .clk(clk), .Q(R_1));  // open: clr
  Register #(.width(16)) R2 (.D(Rd), .en(decoder_1_out2), .clk(clk), .Q(R_2));  // open: clr
  Register #(.width(16)) R3 (.D(Rd), .en(decoder_1_out3), .clk(clk), .Q(R_3));  // open: clr
  Register #(.width(16)) u_R4 (.D(Rd), .en(decoder_1_out4), .clk(clk), .Q(R4));  // open: clr
  Register #(.width(16)) u_R5 (.D(Rd), .en(decoder_1_out5), .clk(clk), .Q(R5));  // open: clr
  Register #(.width(16)) u_R6 (.D(Rd), .en(decoder_1_out6), .clk(clk), .Q(R6));  // open: clr
  Register #(.width(16)) u_R7 (.D(Rd), .en(decoder_1_out7), .clk(clk), .Q(R7));  // open: clr
  Register #(.width(16)) u_R8 (.D(Rd), .en(decoder_1_out8), .clk(clk), .Q(R8));  // open: clr
  Register #(.width(16)) u_R9 (.D(Rd), .en(decoder_1_out9), .clk(clk), .Q(R9));  // open: clr
  Register #(.width(16)) u_R10 (.D(Rd), .en(decoder_1_out10), .clk(clk), .Q(R10));  // open: clr
  Register #(.width(16)) u_R11 (.D(Rd), .en(decoder_1_out11), .clk(clk), .Q(R11));  // open: clr
  Register #(.width(16)) u_R12 (.D(Rd), .en(decoder_1_out12), .clk(clk), .Q(R12));  // open: clr
  Register #(.width(16)) u_R13 (.D(Rd), .en(decoder_1_out13), .clk(clk), .Q(R13));  // open: clr
  Register #(.width(16)) u_R14 (.D(Rd), .en(decoder_1_out14), .clk(clk), .Q(R14));  // open: clr
  Register #(.width(16)) u_R15 (.D(Rd), .en(decoder_1_out15), .clk(clk), .Q(R15));  // open: clr
  Multiplexer #(.select(4), .width(16)) multiplexer_1 (
    .in0({16{1'b0}}), .in1(R_1), .in2(R_2), .in3(R_3), .in4(R4), .in5(R5), .in6(R6), .in7(R7), .in8(R8),
    .in9(R9), .in10(R10), .in11(R11), .in12(R12), .in13(R13), .in14(R14), .in15(R15), .out(Ra), .sel(a));
  Multiplexer #(.select(4), .width(16)) multiplexer_2 (
    .in0({16{1'b0}}), .in1(R_1), .in2(R_2), .in3(R_3), .in4(R4), .in5(R5), .in6(R6), .in7(R7), .in8(R8),
    .in9(R9), .in10(R10), .in11(R11), .in12(R12), .in13(R13), .in14(R14), .in15(R15), .out(Rb), .sel(b));

  // Other names for the same wires on the sheet: R1[15:0] = R_1; R2[15:0] = R_2; R3[15:0] = R_3

  // Notes on the sheet:
  //   R1, R2, R3 as outputs
  //   Selecting which register to send to ALSU for logical stuff
  //   Selecting which register to send to ALSU for logical stuff
endmodule

module flags (
  input  clock,
  input  [4:0] flags_in,
  output [4:0] flags_out
);

  D_Flip_Flop sign (.D(flags_in[0]), .clk(clock), .Q(flags_out[0]));  // open: Qn, preset, reset
  D_Flip_Flop zero (.D(flags_in[1]), .clk(clock), .Q(flags_out[1]));  // open: Qn, preset, reset
  D_Flip_Flop overflow (.D(flags_in[2]), .clk(clock), .Q(flags_out[2]));  // open: Qn, preset, reset
  D_Flip_Flop carry (.D(flags_in[3]), .clk(clock), .Q(flags_out[3]));  // open: Qn, preset, reset
  D_Flip_Flop carry_block (.D(flags_in[4]), .clk(clock), .Q(flags_out[4]));  // open: Qn, preset, reset

  // Other names for the same wires on the sheet: clk = clock; sign = flags_in[0]; zero = flags_in[1];
  //   overflow = flags_in[2]; carry = flags_in[3]; carry_block = flags_in[4]

  // Notes on the sheet:
  //   Flag Bank!
  //   sets flags based on flags_in
endmodule

module ALSU (
  input  [15:0] Ra,
  input  [15:0] Rb,
  input  [15:0] R_d,
  input  [3:0] b,
  input  [3:0] a,
  input  [3:0] d,
  input  [3:0] opcode,
  input  [4:0] flags_in,
  output [15:0] Rd,
  output [4:0] flags_out
);

  wire add_c, add_v, comparator_1_eq, shift_c, sub_c, sub_v;
  wire [4:0] F_SET, FON_FOFF;
  wire [15:0] addition_rd, and_1_out, bit_extender_1_out, LSL, LSR, multiplexer_1_out, multiplier_1_out,
       or_1_out, subtract_rd, xor_1_out;

  assign bit_extender_1_out = {{8{1'b0}}, {a, b}};  // Bit_Extender bit_extender_1
  bit_shifting bit_shifting_1 (.rb(Rb), .LSL(LSL), .carry(shift_c), .LSR(LSR));
  assign and_1_out = Ra & Rb;  // AND_Gate and_1, 16 bits wide
  assign or_1_out = Ra | Rb;  // OR_Gate or_1, 16 bits wide
  add addition (.Ra(Ra), .Rb(Rb), .Rd(addition_rd), .overflow(add_v), .carry(add_c));
  sub subtract (.Ra(Ra), .Rb(Rb), .Rd(subtract_rd), .overflow(sub_v), .carry(sub_c));
  Multiplier #(.width(16)) multiplier_1 (.a(Ra), .b(Rb), .out(multiplier_1_out));  // open: cin, cout
  assign xor_1_out = Ra ^ Rb;  // XOR_Gate xor_1, 16 bits wide
  Multiplexer #(.select(4), .width(16)) multiplexer_1 (
    .in0(LSL), .in1(LSR), .out(multiplexer_1_out), .sel(a));  // open: in2, in3, in4, in5, in6, in7, in8, in9, in10, in11, in12, in13, in14, in15
  Multiplexer #(.select(4), .width(16)) multiplexer_2 (
    .in3(multiplexer_1_out), .in8(and_1_out), .in9(or_1_out), .in10(addition_rd), .in11(subtract_rd),
    .in12(multiplier_1_out), .in13(xor_1_out), .in14(bit_extender_1_out), .in15({a, b, R_d[7:0]}), .out(Rd),
    .sel(opcode));  // open: in0, in1, in2, in4, in5, in6, in7
  Comparator #(.mode("unsigned")) comparator_1 (.a({opcode, a}), .b(8'h36), .eq(comparator_1_eq));  // open: gt, lt
  Multiplexer #(.width(5)) multiplexer_3 (.in0(F_SET), .in1(FON_FOFF), .out(flags_out), .sel(comparator_1_eq));
  FSET fset_1 (
    .opcode(opcode), .Rd(Rd), .add_c(add_c), .sub_c(sub_c), .add_v(add_v), .sub_v(sub_v), .shift_c(shift_c),
    .flags_in(flags_in), .flags_out(F_SET));
  FON_FOFF_logic fon_foff_logic_1 (.a(a), .d(d), .b(b), .opcode(opcode), .flags_in(flags_in), .flags_out(FON_FOFF));

  // Other names for the same wires on the sheet: rd_t[15:0] = R_d; instruction[15:0] = {opcode, d, a, b};
  //   rd_out[15:0] = Rd

  // Notes on the sheet:
  //   setlo
  //   sethigh
  //   Logic for left/right bit shifting
  //   bit shifting
  //   AND
  //   OR
  //   Multiply
  //   XOR
  //   comparing opcode of FON/FOFF
  //   Logic to either set flags using FSET or FON/FOFF based on the OPCODE
endmodule

module FON_FOFF_logic (
  input  [3:0] a,
  input  [3:0] d,
  input  [3:0] b,
  input  [3:0] opcode,
  input  [4:0] flags_in,
  output [4:0] flags_out
);

  wire [4:0] foff, fon, multiplexer_1_out, multiplexer_2_out;

  Multiplexer #(.select(3), .width(5)) multiplexer_1 (
    .in0(fon), .in1(foff), .out(multiplexer_1_out), .sel(d[3:1]));  // open: in2, in3, in4, in5, in6, in7
  Multiplexer #(.select(4), .width(5)) multiplexer_2 (
    .in6(multiplexer_1_out), .out(multiplexer_2_out), .sel(a));  // open: in0, in1, in2, in3, in4, in5, in7, in8, in9, in10, in11, in12, in13, in14, in15
  or or_1 (fon[0], flags_in[0], b[0]);
  or or_2 (fon[1], flags_in[1], b[1]);
  or or_3 (fon[2], flags_in[2], b[2]);
  or or_4 (fon[3], flags_in[3], b[3]);
  or or_5 (fon[4], flags_in[4], d[0]);
  Multiplexer #(.select(4), .width(5)) multiplexer_3 (
    .in3(multiplexer_2_out), .out(flags_out), .sel(opcode));  // open: in0, in1, in2, in4, in5, in6, in7, in8, in9, in10, in11, in12, in13, in14, in15
  and and_1 (foff[0], flags_in[0], b[0]);
  and and_2 (foff[1], flags_in[1], b[1]);
  and and_3 (foff[2], flags_in[2], b[2]);
  and and_4 (foff[3], flags_in[3], b[3]);
  and and_5 (foff[4], flags_in[4], d[0]);

  // Notes on the sheet:
  //   FON logic: using OR to make sure if flags on, stay on & if flags off, turn on
  //   If both Fi and V'i: both 1 then FOFF is 1 otherwise is 0
  //   if both on then stays on, else off
  //   FOFF logic: using AND
endmodule

module bit_shifting (
  input  [15:0] rb,
  output [15:0] LSL,
  output carry,
  output [15:0] LSR
);

  or or_1 (carry, rb[14], rb[1]);

  assign LSL = {rb[14:0], 1'b0};
  assign LSR = {1'b0, rb[15:1]};

  // Notes on the sheet:
  //   Carry if a 1 is shifted out
  //   LSL:
  //   Shifts to the left
  //   LSR: Shifts to the right
  //   Bit shifting logic: 
  //   so the leftmost bit is shifted out and a zero is added to the right
  //   rightmost bit is shifted out and a zero added to front
endmodule

module add (
  input  [15:0] Ra,
  input  [15:0] Rb,
  output [15:0] Rd,
  output overflow,
  output carry
);

  wire adder_1_cout;

  Adder #(.width(15)) adder_1 (.a(Ra[14:0]), .b(Rb[14:0]), .out(Rd[14:0]), .cout(adder_1_cout));  // open: cin
  Adder #(.width(1)) adder_2 (.a(Ra[15]), .b(Rb[15]), .out(Rd[15]), .cin(adder_1_cout), .cout(carry));
  xor xor_1 (overflow, adder_1_cout, carry);

  // Notes on the sheet:
  //   logic for addition
  //   adding an overflow detection!!
  //   : 3 in 1
  //   takes care of addition (using built in subtractors)
  //   carry flag from the carry out of second addition
  //   overflow flag gotten via XOR of previous carry and current carry 
endmodule

module sub (
  input  [15:0] Ra,
  input  [15:0] Rb,
  output [15:0] Rd,
  output overflow,
  output carry
);

  wire subtractor_1_bout;

  Subtractor #(.width(15)) subtractor_1 (
    .a(Ra[14:0]), .b(Rb[14:0]), .out(Rd[14:0]), .bout(subtractor_1_bout));  // open: bin
  Subtractor #(.width(1)) subtractor_2 (.a(Ra[15]), .b(Rb[15]), .out(Rd[15]), .bin(subtractor_1_bout), .bout(carry));
  xor xor_1 (overflow, subtractor_1_bout, carry);

  // Notes on the sheet:
  //   logic for subtraction
  //   adding an overflow detection!!
  //   : 3 in 1
  //   takes care of subtraction (using built in subtractors)
  //   carry flag from the carry out of second subtractor
  //   overflow flag gotten via XOR of previous carry and current carry 
endmodule

module carry_overflow_logic (
  input  [3:0] opcode,
  input  add_carry,
  input  sub_carry,
  input  add_v,
  input  sub_v,
  input  LSL_LSR_c,
  output carry_flag,
  output overflow_flag
);

  wire comparator_1_eq, comparator_2_eq, comparator_3_eq, comparator_4_eq, comparator_5_eq, or_1_out,
       or_2_out, or_3_out, or_4_out;

  Comparator #(.mode("unsigned"), .width(4)) comparator_1 (
    .a(opcode), .b(4'b0011), .eq(comparator_1_eq));  // open: gt, lt
  Comparator #(.mode("unsigned"), .width(4)) comparator_2 (
    .a(opcode), .b(4'b1011), .eq(comparator_2_eq));  // open: gt, lt
  Comparator #(.mode("unsigned"), .width(4)) comparator_3 (
    .a(opcode), .b(4'b1010), .eq(comparator_3_eq));  // open: gt, lt
  or or_1 (or_1_out, add_v, sub_v);
  or or_2 (or_2_out, comparator_2_eq, comparator_3_eq);
  Comparator #(.mode("unsigned"), .width(4)) comparator_4 (
    .a(opcode), .b(4'b1011), .eq(comparator_4_eq));  // open: gt, lt
  Comparator #(.mode("unsigned"), .width(4)) comparator_5 (
    .a(opcode), .b(4'b1010), .eq(comparator_5_eq));  // open: gt, lt
  and and_1 (overflow_flag, or_1_out, or_2_out);
  or or_3 (or_3_out, add_carry, LSL_LSR_c, sub_carry);
  or or_4 (or_4_out, comparator_4_eq, comparator_1_eq, comparator_5_eq);
  and and_2 (carry_flag, or_3_out, or_4_out);

  // Other names for the same wires on the sheet: a_c = add_carry; a_v = add_v; b_c = sub_carry; b_v = sub_v;
  //   shift_c = LSL_LSR_c

  // Notes on the sheet:
  //   logic for carry and overflow flags
  //   making sure correct opcode (if ADD or SUB or shift) else carry will not be triggered
  //   making sure correct opcode (if ADD or SUB) else carry will not be triggered
endmodule

module FSET (
  input  [3:0] opcode,
  input  [15:0] Rd,
  input  add_c,
  input  sub_c,
  input  add_v,
  input  sub_v,
  input  shift_c,
  input  [4:0] flags_in,
  output [4:0] flags_out
);

  Comparator #(.mode("unsigned"), .width(16)) comparator_1 (.a(Rd), .b({16{1'b0}}), .eq(flags_out[1]));  // open: gt, lt
  carry_overflow_logic carry_overflow_logic_1 (
    .opcode(opcode), .add_carry(add_c), .sub_carry(sub_c), .add_v(add_v), .sub_v(sub_v), .LSL_LSR_c(shift_c),
    .carry_flag(flags_out[2]), .overflow_flag(flags_out[3]));

  assign {flags_out[4], flags_out[0]} = {flags_in[4], Rd[15]};

  // Notes on the sheet:
  //   logic for carry & overflow
  //   sign logic
  //   zero logic
  //   CBON()
  //   (since it's set by opcode)
endmodule
